# Fritzing sketch Unihack-arm-prosthetic (saved by Fritzing 0.9.3b)
stripboards: 2

parts:
  DC-DC_stepdown_3A_5V = RioRand LM2596
  Raspberry_Pi1 = Raspberry Pi B+
  PWM1 = PCA9685 16x12-bit PWM Breakout
  Condensator_16V_470uF = Electrolytic Capacitor [capacitance=100µF voltage=16V package="200 mil [THT, electrolytic]"]
  DC1 = DC_DC_XL4016 [chip_label=XL4016 package=board_screw]  # not connected
  DC-DC_stepdown_8A_5_5v = DC_DC_XL4016 [package=board_screw]
  12V_battery = 12 battery [package=battery]  # not connected
  Power_plug1 = USB-C plug
  Servo_1 = Basic Servo
  Servo_2 = Basic Servo
  J1 = Basic Servo  # not connected
  J2 = Basic Servo  # not connected
  J3 = Basic Servo  # not connected
  J4 = Basic Servo  # not connected
  J5 = Basic Servo  # not connected
  J6 = Basic Servo  # not connected

nets:
  N1: DC-DC_stepdown_3A_5V.Pin_1, DC-DC_stepdown_8A_5_5v.IN+
  N2: DC-DC_stepdown_3A_5V.Pin_2, DC-DC_stepdown_8A_5_5v.IN-
  N3: DC-DC_stepdown_3A_5V.Pin_3, Power_plug1.VCC
  N4: DC-DC_stepdown_3A_5V.Pin_4, Power_plug1.GND
  N5: Raspberry_Pi1.GPIO2, PWM1.no_name_yet#504
  N6: Raspberry_Pi1.GPIO3, PWM1.no_name_yet#503
  GND: Raspberry_Pi1.GND, PWM1.no_name_yet#501, PWM1.no_name_yet#701, PWM1.no_name_yet#1000, PWM1.no_name_yet#1001, Condensator_16V_470uF.-, DC-DC_stepdown_8A_5_5v.OUT-, Servo_1.gnd
  N7: Raspberry_Pi1.5V, PWM1.no_name_yet#505
  N8: PWM1.no_name_yet#0, Servo_1.pulse
  N9: PWM1.no_name_yet#1, Servo_2.pulse
  N10: PWM1.no_name_yet#100, PWM1.no_name_yet#101, PWM1.no_name_yet#706, Condensator_16V_470uF.+, DC-DC_stepdown_8A_5_5v.OUT+

custom parts:
  DC_DC_XL4016: DC-DC Converter step down voltage regulator XL4016 custom sketch.
  DC_DC_XL4016: DC-DC Converter step down voltage regulator XL4016 custom sketch.
  12 battery: 12V lead acid type battery, like the Husqvarna YTH2448 12V 35AH battery. This is the mini version 1/4 the size of the actual battery to be closer to typical breadboard parts (around 2in wide rathher than 7in). The pads in pcb are sized to accomidate up to 14ga wire (as these batterys will deliver high currents.)
  USB-C plug: power plug
